// Logisim project CS1501_U201514477_华龙_cpu.circ as structural Verilog: 3 circuits, main circuit MIPS CPU
module MIPS_CPU (
);

  wire ALU_Equal, ALU_R_0, and_1_out, and_2_out, and_3_out, beq, bltz, bne, branch, button_1_out, clk,
       d_ff_1_q;
  wire [3:0] ALUOP;
  wire [4:0] multiplexer_4_out, multiplexer_5_out, multiplexer_6_out, multiplexer_7_out;
  wire [15:0] multiplexer_17_out;
  wire [16:0] multiplexer_8_out, multiplexer_9_out, multiplexer_10_out;
  wire [23:0] control_signal;
  wire [27:2] rom_1_data;
  wire [31:0] adder_1_out, bit_extender_1_out, mips_ram_1_p5, multiplexer_1_out, multiplexer_2_out,
       multiplexer_3_out, multiplexer_11_out, multiplexer_12_out, multiplexer_13_out, multiplexer_14_out, PC,
       PC_1, pull_resistor_1_node, pull_resistor_2_node, RF_A, RF_B, rom_1_data_2, \数码管锁存_q ;
  wire [31:1] alu_1_result;

  Multiplexer #(.width(32), .enable("false")) multiplexer_1 (
    .in0(multiplexer_2_out), .in1(multiplexer_3_out), .out(multiplexer_1_out), .sel(control_signal[9]));
  Multiplexer #(.width(32), .enable("false")) multiplexer_2 (
    .in0(PC_1), .in1(adder_1_out), .out(multiplexer_2_out), .sel(branch));
  Multiplexer #(.width(32), .enable("false")) multiplexer_3 (
    .in0({PC_1[31:28], rom_1_data, 2'b00}), .in1(RF_A), .out(multiplexer_3_out), .sel(control_signal[8]));
  PC_1 pc_1_1 (.PC(PC), .PC_4(PC_1));
  Register #(.width(32)) u_PC (.D(multiplexer_1_out), .en(d_ff_1_q), .Q(PC), .clk(clk), .clr(button_1_out));
  Button button_1 (.out(button_1_out));
  Register #(.width(32)) \u_数码管锁存  (.D(RF_B), .en(control_signal[4]), .Q(\数码管锁存_q ), .clk(clk));  // open: clr
  D_Flip_Flop d_ff_1 (.clk(clk), .Q(d_ff_1_q));  // open: D, Qn, preset, en, reset
  Hex_Digit_Display hex_digit_display_1 (.value(\数码管锁存_q [27:24]));  // open: dp
  Hex_Digit_Display hex_digit_display_2 (.value(\数码管锁存_q [31:28]));  // open: dp
  ROM #(.addrWidth(24), .dataWidth(32)) rom_1 (
    .addr(PC[25:2]), .data({rom_1_data_2[31:28], rom_1_data, rom_1_data_2[1:0]}));  // open: sel
  Hex_Digit_Display hex_digit_display_3 (.value(\数码管锁存_q [19:16]));  // open: dp
  Hex_Digit_Display hex_digit_display_4 (.value(\数码管锁存_q [23:20]));  // open: dp
  Hex_Digit_Display hex_digit_display_5 (.value(\数码管锁存_q [11:8]));  // open: dp
  Hex_Digit_Display hex_digit_display_6 (.value(\数码管锁存_q [15:12]));  // open: dp
  MIPS_Controller mips_controller_1 (
    .OP({rom_1_data_2[31:28], rom_1_data[27:26]}), .Funct({rom_1_data[5:2], rom_1_data_2[1:0]}),
    .\控制信号 ({ALUOP, control_signal[23:8], beq, bne, bltz, control_signal[4:0]}));
  Multiplexer #(.width(5), .enable("false")) multiplexer_4 (
    .in0(rom_1_data[20:16]), .in1(rom_1_data[15:11]), .out(multiplexer_4_out), .sel(control_signal[21]));
  Hex_Digit_Display hex_digit_display_7 (.value(\数码管锁存_q [7:4]));  // open: dp
  Hex_Digit_Display hex_digit_display_8 (.value(\数码管锁存_q [3:0]));  // open: dp
  Multiplexer #(.width(5), .enable("false")) multiplexer_5 (
    .in0(rom_1_data[25:21]), .in1(5'b00010), .out(multiplexer_5_out), .sel(control_signal[23]));
  Multiplexer #(.width(5), .enable("false")) multiplexer_6 (
    .in0(rom_1_data[20:16]), .in1(5'b00100), .out(multiplexer_6_out), .sel(control_signal[22]));
  Multiplexer #(.width(5), .enable("false")) multiplexer_7 (
    .in0(multiplexer_4_out), .in1({5{1'b1}}), .out(multiplexer_7_out), .sel(control_signal[20]));
  Multiplexer #(.width(17), .enable("false")) multiplexer_8 (
    .in0(17'ha), .in1({{12{1'b0}}, rom_1_data[10:6]}), .out(multiplexer_8_out), .sel(control_signal[12]));
  Multiplexer #(.width(17), .enable("false")) multiplexer_9 (
    .in0(multiplexer_8_out), .in1(multiplexer_10_out), .out(multiplexer_9_out), .sel(control_signal[11]));
  Multiplexer #(.width(17), .enable("false")) multiplexer_10 (
    .in0({{2{rom_1_data[15]}}, rom_1_data[14:2], rom_1_data_2[1:0]}),
    .in1({1'b0, rom_1_data[15:2], rom_1_data_2[1:0]}), .out(multiplexer_10_out), .sel(control_signal[10]));
  Multiplexer #(.width(32), .enable("false")) multiplexer_11 (
    .in0({alu_1_result, ALU_R_0}), .in1(PC_1), .out(multiplexer_11_out), .sel(control_signal[18]));
  Multiplexer #(.width(32), .enable("false")) multiplexer_12 (
    .in0(multiplexer_11_out), .in1(multiplexer_13_out), .out(multiplexer_12_out), .sel(control_signal[17]));
  Multiplexer #(.width(32), .enable("false")) multiplexer_13 (
    .in0(mips_ram_1_p5), .in1({{16{1'b0}}, multiplexer_17_out}), .out(multiplexer_13_out),
    .sel(control_signal[16]));
  assign bit_extender_1_out = {{15{multiplexer_9_out[16]}}, multiplexer_9_out};  // Bit_Extender bit_extender_1
  // RegisterFile registerfile_1: pin names not known; wires that end beside it: multiplexer_12_out, clk, control_signal[19], multiplexer_7_out, multiplexer_5_out, multiplexer_6_out, RF_A, RF_B
  Multiplexer #(.width(32), .enable("false")) multiplexer_14 (
    .in0(RF_B), .in1(RF_A), .out(multiplexer_14_out), .sel(control_signal[14]));
  Adder #(.width(32)) adder_1 (.a(PC), .b({bit_extender_1_out[29:0], 2'b00}), .out(adder_1_out));  // open: cin, cout
  Pull_Resistor pull_resistor_1 (.node(pull_resistor_1_node));
  Multiplexer #(.width(32), .enable("false")) multiplexer_15 (
    .in0(RF_A), .in1(RF_B), .out(pull_resistor_1_node), .sel(control_signal[15]));
  Pull_Resistor pull_resistor_2 (.node(pull_resistor_2_node));
  Multiplexer #(.width(32), .enable("false")) multiplexer_16 (
    .in0(multiplexer_14_out), .in1(bit_extender_1_out), .out(pull_resistor_2_node), .sel(control_signal[13]));
  Pull_Resistor #(.pull(1)) pull_resistor_3 (.node(ALUOP));
  // MIPS_RAM mips_ram_1: pin names not known; wires that end beside it: alu_1_result[25:2], RF_B, control_signal[3], clk, mips_ram_1_p5
  // Probe on mips_ram_1_p5
  ALU alu_1 (
    .AluOP(ALUOP), .X(pull_resistor_1_node), .Equal(ALU_Equal), .Result({alu_1_result, ALU_R_0}),
    .Y(pull_resistor_2_node));  // open: Signed_Overflow, Result_2, UnSigned_Overflow
  Multiplexer #(.width(16), .enable("false")) multiplexer_17 (
    .in0(mips_ram_1_p5[15:0]), .in1(mips_ram_1_p5[31:16]), .out(multiplexer_17_out), .sel(alu_1_result[1]));
  and and_1 (and_1_out, ALU_Equal, beq);
  and and_2 (and_2_out, ~ALU_Equal, bne);  // AND_Gate
  and and_3 (and_3_out, ALU_R_0, bltz);
  or or_1 (branch, and_1_out, and_2_out, and_3_out);

  // Other names for the same wires on the sheet: DM_WE = control_signal[3]; display__a0 = control_signal[4];
  //   control_signal (some bits) = {ALUOP, beq, bne, bltz}; jump_register = control_signal[8];
  //   jump = control_signal[9]; zero_ext_IMM = control_signal[10]; extend_IMM = control_signal[11];
  //   extend_shamt = control_signal[12]; Y__S_EXT = control_signal[13]; Y__RF_A = control_signal[14];
  //   X__RF_B = control_signal[15]; Din__DM_half = control_signal[16]; Din__DM = control_signal[17];
  //   Din__PC_1 = control_signal[18]; RF_WE = control_signal[19]; rW__GPR_31 = control_signal[20];
  //   rW__rd = control_signal[21]; rB___a0 = control_signal[22]; rA___v0 = control_signal[23]

  // Notes on the sheet:
  //   contents of rom_1 (hex, n*v repeats v):
  //   c
endmodule

module PC_1 (
  input  [31:0] PC,
  output [31:0] PC_4
);

  // Incrementer incrementer_1: pin names not known; wires that end beside it: PC[31:2], PC_4[31:2]

  assign PC_4[1:0] = PC[1:0];
endmodule

module MIPS_Controller (
  input  [5:0] OP,
  input  [5:0] Funct,
  output [27:0] \控制信号 
);

  ROM #(.addrWidth(12), .dataWidth(28)) rom_1 (.addr({OP, Funct}), .data(\控制信号 ));  // open: sel

  // Notes on the sheet:
  //   contents of rom_1 (hex, n*v repeats v):
  //   28b000 0 228b000 128b000 0 0 228c000 0 300 0 0 0 6c02010 19*0 5280000 5280000 6280000 0 7280000
  //   8280000 0 a280000 0 0 b280000 c280000 20*0 64*b000820 64*200 64*1c0200 64*880 64*840 128*0
  //   128*5082800 64*b082800 64*c082800 64*7082c00 64*8082c00 1216*0 64*50b2800 64*0 64*50a2800 448*0
  //   64*5002808
endmodule
